# Fritzing sketch airware (saved by Fritzing 0.9.3b)
circuit board: 7.04597cm x 5.61101cm
breadboards: 1

parts:
  R5 = Resistor [tolerance=±5% resistance=10k package=THT]
  R6 = Resistor [tolerance=±5% resistance=10k package=THT]
  J1 = double row female pin header, 16 pins [form="♀ (female)" part_number="output board conn"]
  JP1 = Header 2 [package=jst-2-pth]
  J2 = female pin header, 12 pins [form="♀ (female)" part_number="feather lora small"]
  J3 = female pin header, 16 pins [form="♀ (female)" part_number="feather lora big"]
  J4 = female pin header, 12 pins [form="♀ (female)" part_number="feather output small"]
  J5 = female pin header, 16 pins [form="♀ (female)" part_number="feather output big"]

nets:
  N1: R5.Pin_0, J1.pin3, J2.pin11, J4.pin11
  N2: R5.Pin_1, R6.Pin_1, J3.pin2
  N3: R6.Pin_0, J1.pin4, J2.pin12, J4.pin12
  N4: J1.pin1, JP1.2, J3.pin4, J5.pin4
  N5: J1.pin2, J5.pin2
  N6: J1.pin5, J5.pin11
  N7: J1.pin6, J5.pin12
  N8: J1.pin7, J5.pin13
  N9: J1.pin8, J4.pin10
  N10: J1.pin9, J4.pin9
  N11: J1.pin10, J4.pin8
  N12: J1.pin11, J4.pin7
  N13: J1.pin12, J4.pin6
  N14: J1.pin13, J4.pin5
  N15: J1.pin14, J4.pin4
  N16: J1.pin15, J5.pin6
  N17: J1.pin16, J5.pin5
  N18: JP1.1, J2.pin1, J4.pin1
  N19: J2.pin9, J3.pin16

notes:
  for connecting the battery and the solar charger we would obviously use the JST ports
  on both the charger as well as the feaher boards
  feather lora
  feather output
