# Fritzing sketch airware_POC (saved by Fritzing 0.9.3b)
breadboards: 1

parts:
  Part1 = Adafruit Feather 32u4 RFM9xW LoRa [part_number="Adafruit #3078 and Adafruit #3079"]
  Part2 = Adafruit Feather 32u4 Adalogger [part_number="Adafruit #2795"]
  ANT1 = Antenna
  LED1 = LED - 5mm [color="Red (633nm)" package="5 mm [THT]"]
  LED2 = LED - 5mm [color="Red (633nm)" package="5 mm [THT]"]
  LED3 = LED - 5mm [color="Red (633nm)" package="5 mm [THT]"]
  LED4 = LED - 5mm [color="Red (633nm)" package="5 mm [THT]"]
  R1 = Resistor [tolerance=±5% resistance=1k package=THT]
  R2 = Resistor [tolerance=±5% resistance=1k package=THT]
  R3 = Resistor [tolerance=±5% resistance=1k package=THT]
  R4 = Resistor [tolerance=±5% resistance=1k package=THT]
  R5 = Resistor [tolerance=±5% resistance=10k package=THT]
  R6 = Resistor [tolerance=±5% resistance=10k package=THT]
  Part3 = Adafruit USB DC Solar LiPo Charger [part_number="Adafruit #390"]
  U1 = LIPO-2000mAh [package=lipo-2000]

nets:
  N1: Part1.ANT, ANT1.antenna_lead
  N2: Part1.DIO1, Part1.6
  GND: Part1.GND, Part2.GND, LED1.cathode, LED2.cathode, LED3.cathode, LED4.cathode, Part3.GND, U1.-
  N3: Part1.+3V3, R5.Pin_1, R6.Pin_1
  N4: Part1.VBAT, Part2.VBAT, Part3.LOAD
  N5: Part1.3, Part2.3, R5.Pin_0
  N6: Part1.2, Part2.2, R6.Pin_0
  N7: Part2.12, R4.Pin_1
  N8: Part2.11, R3.Pin_1
  N9: Part2.10, R2.Pin_1
  N10: Part2.9, R1.Pin_1
  N11: LED1.anode, R4.Pin_0
  N12: LED2.anode, R3.Pin_0
  N13: LED3.anode, R2.Pin_0
  N14: LED4.anode, R1.Pin_0
  N15: Part3.BATT, U1.+

notes:
  for connecting the battery and the solar charger we would obviously use the JST ports
  on both the charger as well as the feaher boards

custom parts:
  Adafruit Feather 32u4 RFM9xW LoRa: This is the Adafruit Feather 32u4 LoRa Radio (RFM9x) - our take on an microcontroller with a "Long Range (LoRa)" packet radio transceiver with built in USB and battery charging. Its an Adafruit Feather 32u4 with a 868/915 MHz radio module cooked in! Great for making wireless networks that can go further than 2.4GHz 802.15.4 and similar, are more flexible than Bluetooth LE and without the high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
  Adafruit Feather 32u4 Adalogger: This is the Adafruit Feather 32u4 Adalogger - our take on an 'all-in-one' datalogger (or data-reader) with built in USB and battery charging. Its an Adafruit Feather 32u4 with a microSD holder ready to rock! We have other boards in the Feather family, check'em out here At the Feather 32u4's heart is at ATmega32u4 clocked at 8 MHz and at 3.3V logic, a chip setup we've had tons of experience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
  Adafruit USB DC Solar LiPo Charger: Make your projects to go green this summer with our specialized USB/Solar Lithium Ion Polymer Battery charger! This charger is a very unique design, perfect for outdoor projects, or DIY iPod chargers. We've spent over a year testing and tinkering with this charger to come up with a plug and play solution to charging batteries with the sun and we're really pleased with what we ended up with.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
