# Fritzing sketch airware_POC2 (saved by Fritzing 0.9.3b)
breadboards: 2

parts:
  Part1 = Adafruit Feather 32u4 RFM9xW LoRa [part_number="Adafruit #3078 and Adafruit #3079"]
  Part2 = Adafruit Feather 32u4 Adalogger [part_number="Adafruit #2795"]
  ANT1 = Antenna
  LED1 = LED - 5mm [color="Red (633nm)" package="5 mm [THT]"]
  LED2 = LED - 5mm [color="Red (633nm)" package="5 mm [THT]"]
  LED3 = LED - 5mm [color="Red (633nm)" package="5 mm [THT]"]
  LED4 = LED - 5mm [color="Red (633nm)" package="5 mm [THT]"]
  R1 = Resistor [tolerance=±5% resistance=1k package=THT]
  R2 = Resistor [tolerance=±5% resistance=1k package=THT]
  R3 = Resistor [tolerance=±5% resistance=1k package=THT]
  R4 = Resistor [tolerance=±5% resistance=1k package=THT]
  R5 = Resistor [tolerance=±5% resistance=10k package=THT]
  R6 = Resistor [tolerance=±5% resistance=10k package=THT]
  Part3 = Adafruit USB DC Solar LiPo Charger [part_number="Adafruit #390"]
  U1 = LIPO-2000mAh [package=lipo-2000]
  J3 = female pin header, 2 pins [form="♀ (female)" part_number=TP_out]  # not connected
  J4 = female pin header, 2 pins [form="♀ (female)" part_number=TP_in]  # not connected
  JP3 = Header 2 [part_number=OUT package=molex-1x2_lock]  # not connected
  JP4 = Header 2 [part_number=IN package=molex-1x2_lock]  # not connected
  R7 = Resistor [tolerance=±5% resistance=47k package=THT]
  R8 = Resistor [tolerance=±5% resistance=82k package=THT]
  R9 = Resistor [tolerance=±5% resistance=15k package=THT]
  R10 = Resistor [tolerance=±5% resistance=16k package=THT]
  R11 = Resistor [tolerance=±5% resistance=220 package=THT]
  R12 = Resistor [tolerance=±5% resistance=560 package=THT]  # not connected
  D2 = Zener Diode [part_number=1N5221B breakdown_voltage=2.4V package="300 mil [THT]"]
  IC2 = IC, DIP package, 8 pins [chip_label=LM393]
  Part4 = Adafruit Precision RTC FeatherWing [part_number="Adafruit #3028"]
  R13 = Resistor [tolerance=±5% resistance=560 package=THT]

nets:
  N1: Part1.ANT, ANT1.antenna_lead
  N2: Part1.DIO1, Part1.6
  GND: Part1.GND, Part2.GND, LED1.cathode, LED2.cathode, LED3.cathode, LED4.cathode, Part3.GND, U1.-, R9.Pin_1, D2.anode, Part4.I
  N3: Part1.+3V3, R5.Pin_1, R6.Pin_1
  N4: Part1.VBAT, Part3.LOAD, R8.Pin_1, R11.Pin_0
  N5: Part1.EN, Part2.EN, Part4.SCK, R13.Pin_1
  N6: Part1.3, Part2.3, R5.Pin_0, Part4.3.3V
  N7: Part1.2, Part2.2, R6.Pin_0, Part4.RESET
  N8: Part2.MOSI, Part4.VBAT
  N9: Part2.SCK, Part4.EN
  N10: Part2.A5, Part4.USB
  N11: Part2.A4, Part4.N
  N12: Part2.A3, Part4.M
  N13: Part2.A2, Part4.L
  N14: Part2.A1, Part4.K
  N15: Part2.A0, Part4.J
  N16: Part2.AREF, Part4.H
  N17: Part2.+3V3, Part4.SCL
  N18: Part2.RST, Part4.SDA
  N19: Part2.VBAT, Part4.MOSI
  N20: Part2.VBUS, Part4.F
  N21: Part2.13, Part4.E
  N22: Part2.12, R4.Pin_1, Part4.D
  N23: Part2.11, R3.Pin_1, Part4.C
  N24: Part2.10, Part4.B, Part4.SQW
  N25: Part2.9, Part4.A
  N26: Part2.6, R2.Pin_1, Part4.GND
  N27: Part2.5, R1.Pin_1, Part4.AREF
  N28: LED1.anode, R4.Pin_0
  N29: LED2.anode, R3.Pin_0
  N30: LED3.anode, R2.Pin_0
  N31: LED4.anode, R1.Pin_0
  N32: Part3.BATT, U1.+
  N33: R7.Pin_1, R8.Pin_0, IC2.pin5
  N34: R9.Pin_0, R10.Pin_1, IC2.pin6
  N35: R10.Pin_0, R11.Pin_1, D2.cathode
  N36: IC2.pin7, R13.Pin_0

notes:
  for connecting the battery and the solar charger we would obviously use the JST ports
  on both the charger as well as the feaher boards

custom parts:
  Adafruit Feather 32u4 RFM9xW LoRa: This is the Adafruit Feather 32u4 LoRa Radio (RFM9x) - our take on an microcontroller with a "Long Range (LoRa)" packet radio transceiver with built in USB and battery charging. Its an Adafruit Feather 32u4 with a 868/915 MHz radio module cooked in! Great for making wireless networks that can go further than 2.4GHz 802.15.4 and similar, are more flexible than Bluetooth LE and without the high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
  Adafruit Feather 32u4 Adalogger: This is the Adafruit Feather 32u4 Adalogger - our take on an 'all-in-one' datalogger (or data-reader) with built in USB and battery charging. Its an Adafruit Feather 32u4 with a microSD holder ready to rock! We have other boards in the Feather family, check'em out here At the Feather 32u4's heart is at ATmega32u4 clocked at 8 MHz and at 3.3V logic, a chip setup we've had tons of experience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
  Adafruit USB DC Solar LiPo Charger: Make your projects to go green this summer with our specialized USB/Solar Lithium Ion Polymer Battery charger! This charger is a very unique design, perfect for outdoor projects, or DIY iPod chargers. We've spent over a year testing and tinkering with this charger to come up with a plug and play solution to charging batteries with the sun and we're really pleased with what we ended up with.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
  Adafruit Precision RTC FeatherWing: A Feather board without ambition is a Feather board without FeatherWings! This is the DS3231 Precision RTC FeatherWing: it adds an extremely accurate I2C-integrated Real Time Clock (RTC) with a Temperature Compensated Crystal Oscillator (TCXO) to any Feather main board. This RTC is the most precise you can get in a small, low power package. Using our Feather Stacking Headers or Feather Female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
