# Fritzing sketch airware_POC3 (saved by Fritzing 0.9.3b)
breadboards: 2

parts:
  Part2 = Adafruit Feather 32u4 Adalogger [part_number="Adafruit #2795"]
  ANT1 = Antenna
  R12 = Resistor [tolerance=±5% resistance=560 package=THT]
  Part4 = Adafruit Precision RTC FeatherWing [part_number="Adafruit #3028"]
  Part5 = Adafruit Feather 32u4 RFM9xW LoRa [part_number="Adafruit #3078 and Adafruit #3079"]
  IC3 = IC, DIP package, 8 pins [chip_label=LM393]
  Part6 = Adafruit USB DC Solar LiPo Charger [part_number="Adafruit #390"]
  Q1 = NPN-Transistor [part_number=BC548 package="SOT-23 [SMD]"]
  R14 = Resistor [tolerance=±5% resistance=220 package=THT]
  D3 = Zener Diode [part_number=1N5221B breakdown_voltage=2.4V package="300 mil [THT]"]
  R15 = Resistor [tolerance=±5% resistance=16k package=THT]
  R16 = Resistor [tolerance=±5% resistance=18k package=THT]
  R17 = Resistor [tolerance=±5% resistance=10k package=THT]
  R18 = Resistor [tolerance=±5% resistance=16k package=THT]
  R19 = Resistor [tolerance=±5% resistance=10k package=THT]
  R20 = Resistor [tolerance=±5% resistance=15k package=THT]
  R21 = Resistor [tolerance=±5% resistance=10k package=THT]
  R22 = Resistor [tolerance=±5% resistance=10k package=THT]
  R23 = Resistor [tolerance=±5% resistance=10k package=THT]
  LED5 = LED - 5mm [color="Red (633nm)" package="5 mm [THT]"]
  LED6 = LED - 5mm [color="Red (633nm)" package="5 mm [THT]"]
  LED7 = LED - 5mm [color="Red (633nm)" package="5 mm [THT]"]
  LED8 = LED - 5mm [color="Red (633nm)" package="5 mm [THT]"]
  R24 = Resistor [tolerance=±5% resistance=1k package=THT]
  R25 = Resistor [tolerance=±5% resistance=1k package=THT]
  R26 = Resistor [tolerance=±5% resistance=1k package=THT]
  R27 = Resistor [tolerance=±5% resistance=1k package=THT]
  R28 = Resistor [tolerance=±5% resistance=2.2k package=THT]
  R29 = Resistor [tolerance=±5% resistance=2.2k package=THT]

nets:
  GND: Part2.GND, Part4.G, Part4.GND, Part5.GND, IC3.pin4, Q1.1, LED5.cathode, LED6.cathode, LED7.cathode, LED8.cathode
  N1: Part2.1, Part4.TX
  N2: Part2.0, Part4.RX
  N3: Part2.MISO, Part4.MISO
  N4: Part2.MOSI, Part4.MOSI
  N5: Part2.SCK, Part4.SCK
  N6: Part2.A5, Part4.F
  N7: Part2.A4, Part4.E
  N8: Part2.A3, Part4.D
  N9: Part2.A2, Part4.C
  N10: Part2.A1, Part4.B
  N11: Part2.A0, Part4.A
  N12: Part2.AREF, Part4.AREF
  +3V3: Part2.+3V3, Part4.3.3V, R28.Pin_0, R29.Pin_0
  N13: Part2.RST, Part4.RESET
  N14: Part2.VBAT, Part4.VBAT, Part5.VBAT, IC3.pin8
  N15: Part2.EN, Part4.EN, Part5.EN, Q1.2
  N16: Part2.VBUS, Part4.USB
  N17: Part2.13, Part4.N
  N18: Part2.12, Part4.M, R24.Pin_1
  N19: Part2.11, Part4.L, R25.Pin_1
  N20: Part2.10, Part4.SQW, Part4.K
  N21: Part2.9, Part4.J, R27.Pin_1
  N22: Part2.6, Part4.I, Part5.12, R23.Pin_1
  N23: Part2.5, Part4.H, R26.Pin_1
  N24: Part2.3, Part4.SCL, Part5.3, R28.Pin_1
  N25: Part2.2, Part4.SDA, Part5.2, R29.Pin_1
  N26: ANT1.antenna_lead, Part5.ANT
  N27: R12.Pin_0, Q1.0
  N28: R12.Pin_1, IC3.pin1, R20.Pin_1
  N29: Part5.DIO1, Part5.6
  N30: Part5.A4, R21.Pin_1, R22.Pin_1
  N31: IC3.pin2, R15.Pin_0, R16.Pin_1
  N32: IC3.pin3, R19.Pin_0, R20.Pin_0
  N33: Part6.BATT, R14.Pin_0, R18.Pin_0, R21.Pin_0
  N34: Part6.GND, D3.anode, R16.Pin_0, R17.Pin_0, R22.Pin_0, R23.Pin_0
  N35: R14.Pin_1, D3.cathode, R15.Pin_1
  N36: R17.Pin_1, R18.Pin_1, R19.Pin_1
  N37: LED5.anode, R24.Pin_0
  N38: LED6.anode, R25.Pin_0
  N39: LED7.anode, R27.Pin_0
  N40: LED8.anode, R26.Pin_0

notes:
  KEEP IN MIND THERE IS A FEATHER BELOW THE RTC
  MAKE SURE TO CONNECT THE LOAD AND BATTERY MEASURE POITN AS SHOWN!

custom parts:
  Adafruit Feather 32u4 Adalogger: This is the Adafruit Feather 32u4 Adalogger - our take on an 'all-in-one' datalogger (or data-reader) with built in USB and battery charging. Its an Adafruit Feather 32u4 with a microSD holder ready to rock! We have other boards in the Feather family, check'em out here At the Feather 32u4's heart is at ATmega32u4 clocked at 8 MHz and at 3.3V logic, a chip setup we've had tons of experience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
  Adafruit Precision RTC FeatherWing: A Feather board without ambition is a Feather board without FeatherWings! This is the DS3231 Precision RTC FeatherWing: it adds an extremely accurate I2C-integrated Real Time Clock (RTC) with a Temperature Compensated Crystal Oscillator (TCXO) to any Feather main board. This RTC is the most precise you can get in a small, low power package. Using our Feather Stacking Headers or Feather Female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
  Adafruit Feather 32u4 RFM9xW LoRa: This is the Adafruit Feather 32u4 LoRa Radio (RFM9x) - our take on an microcontroller with a "Long Range (LoRa)" packet radio transceiver with built in USB and battery charging. Its an Adafruit Feather 32u4 with a 868/915 MHz radio module cooked in! Great for making wireless networks that can go further than 2.4GHz 802.15.4 and similar, are more flexible than Bluetooth LE and without the high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
  Adafruit USB DC Solar LiPo Charger: Make your projects to go green this summer with our specialized USB/Solar Lithium Ion Polymer Battery charger! This charger is a very unique design, perfect for outdoor projects, or DIY iPod chargers. We've spent over a year testing and tinkering with this charger to come up with a plug and play solution to charging batteries with the sun and we're really pleased with what we ended up with.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
