# Fritzing sketch airware_POC4 (saved by Fritzing 0.9.3b)
breadboards: 2

parts:
  ANT1 = Antenna
  R12 = Resistor [tolerance=±5% resistance=560 package=THT]
  Part4 = Adafruit Precision RTC FeatherWing [part_number="Adafruit #3028"]  # not connected
  Part5 = Adafruit Feather 32u4 RFM9xW LoRa [part_number="Adafruit #3078 and Adafruit #3079"]
  IC3 = IC, DIP package, 8 pins [chip_label=LM393]
  Part6 = Adafruit USB DC Solar LiPo Charger [part_number="Adafruit #390"]
  Q1 = NPN-Transistor [part_number=BC548 package="SOT-23 [SMD]"]
  R14 = Resistor [tolerance=±5% resistance=220 package=THT]
  D3 = Zener Diode [part_number=1N5221B breakdown_voltage=2.4V package="300 mil [THT]"]
  R15 = Resistor [tolerance=±5% resistance=16k package=THT]
  R16 = Resistor [tolerance=±5% resistance=18k package=THT]
  R17 = Resistor [tolerance=±5% resistance=10k package=THT]
  R18 = Resistor [tolerance=±5% resistance=16k package=THT]
  R19 = Resistor [tolerance=±5% resistance=10k package=THT]
  R20 = Resistor [tolerance=±5% resistance=15k package=THT]
  R21 = Resistor [tolerance=±5% resistance=10k package=THT]
  R22 = Resistor [tolerance=±5% resistance=10k package=THT]
  LED5 = LED - 5mm [color="Red (633nm)" package="5 mm [THT]"]
  LED6 = LED - 5mm [color="Red (633nm)" package="5 mm [THT]"]
  LED7 = LED - 5mm [color="Red (633nm)" package="5 mm [THT]"]
  LED8 = LED - 5mm [color="Red (633nm)" package="5 mm [THT]"]
  R24 = Resistor [tolerance=±5% resistance=220 package=THT]
  R25 = Resistor [tolerance=±5% resistance=220 package=THT]
  R26 = Resistor [tolerance=±5% resistance=220 package=THT]
  R27 = Resistor [tolerance=±5% resistance=220 package=THT]
  LED9 = LED - 5mm [color="Red (633nm)" package="5 mm [THT]"]
  R28 = Resistor [tolerance=±5% resistance=220 package=THT]
  R29 = Resistor [tolerance=±5% resistance=220 package=THT]
  LED10 = LED - 5mm [color="Red (633nm)" package="5 mm [THT]"]
  LED11 = LED - 5mm [color="Red (633nm)" package="5 mm [THT]"]
  R30 = Resistor [tolerance=±5% resistance=220 package=THT]
  R31 = Resistor [tolerance=±5% resistance=220 package=THT]
  LED12 = LED - 5mm [color="Red (633nm)" package="5 mm [THT]"]
  LED13 = LED - 5mm [color="Red (633nm)" package="5 mm [THT]"]
  R32 = Resistor [tolerance=±5% resistance=220 package=THT]
  R33 = Resistor [tolerance=±5% resistance=220 package=THT]
  LED14 = LED - 5mm [color="Red (633nm)" package="5 mm [THT]"]
  J1 = Basic Servo

nets:
  N1: ANT1.antenna_lead, Part5.ANT
  N2: R12.Pin_0, Q1.0
  N3: R12.Pin_1, IC3.pin1, R20.Pin_1
  N4: Part5.DIO1, Part5.6
  N5: Part5.A5, R33.Pin_1
  N6: Part5.A4, R21.Pin_1, R22.Pin_1
  N7: Part5.A3, R32.Pin_1
  N8: Part5.A2, R31.Pin_1
  N9: Part5.A1, R30.Pin_1
  N10: Part5.A0, R29.Pin_1
  GND: Part5.GND, IC3.pin4, Q1.1, LED6.cathode, LED7.cathode, LED8.cathode, LED9.cathode, LED10.cathode, LED11.cathode, LED12.cathode, LED13.cathode, LED14.cathode, J1.gnd
  N11: Part5.VBAT, IC3.pin8, J1.vcc
  N12: Part5.EN, Q1.2
  N13: Part5.13, R28.Pin_1
  N14: Part5.12, R26.Pin_1
  N15: Part5.11, J1.pulse
  N16: Part5.10, R27.Pin_1
  N17: Part5.9, R25.Pin_1
  N18: Part5.5, R24.Pin_1
  N19: IC3.pin2, R15.Pin_0, R16.Pin_1
  N20: IC3.pin3, R19.Pin_0, R20.Pin_0
  N21: Part6.BATT, R14.Pin_0, R18.Pin_0, R21.Pin_0
  N22: Part6.GND, D3.anode, R16.Pin_0, R17.Pin_0, R22.Pin_0
  N23: R14.Pin_1, D3.cathode, R15.Pin_1
  N24: R17.Pin_1, R18.Pin_1, R19.Pin_1
  N25: LED5.anode, R24.Pin_0
  N26: LED6.anode, R25.Pin_0
  N27: LED7.anode, R27.Pin_0
  N28: LED8.anode, R26.Pin_0
  N29: LED9.anode, R29.Pin_0
  N30: R28.Pin_0, LED10.anode
  N31: LED11.anode, R31.Pin_0
  N32: R30.Pin_0, LED12.anode
  N33: LED13.anode, R33.Pin_0
  N34: R32.Pin_0, LED14.anode

notes:
  KEEP IN MIND THERE IS A FEATHER BELOW THE RTC
  MAKE SURE TO CONNECT THE LOAD AND BATTERY MEASURE POITN AS SHOWN!

custom parts:
  Adafruit Precision RTC FeatherWing: A Feather board without ambition is a Feather board without FeatherWings! This is the DS3231 Precision RTC FeatherWing: it adds an extremely accurate I2C-integrated Real Time Clock (RTC) with a Temperature Compensated Crystal Oscillator (TCXO) to any Feather main board. This RTC is the most precise you can get in a small, low power package. Using our Feather Stacking Headers or Feather Female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
  Adafruit Feather 32u4 RFM9xW LoRa: This is the Adafruit Feather 32u4 LoRa Radio (RFM9x) - our take on an microcontroller with a "Long Range (LoRa)" packet radio transceiver with built in USB and battery charging. Its an Adafruit Feather 32u4 with a 868/915 MHz radio module cooked in! Great for making wireless networks that can go further than 2.4GHz 802.15.4 and similar, are more flexible than Bluetooth LE and without the high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
  Adafruit USB DC Solar LiPo Charger: Make your projects to go green this summer with our specialized USB/Solar Lithium Ion Polymer Battery charger! This charger is a very unique design, perfect for outdoor projects, or DIY iPod chargers. We've spent over a year testing and tinkering with this charger to come up with a plug and play solution to charging batteries with the sun and we're really pleased with what we ended up with.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
